// Logisim project Kaysarul_Anas_lab_07.circ as structural Verilog: 4 circuits, main circuit main
module main (
  input  in_1,
  output [15:0] Output,
  output [15:0] out_3,
  output out_4,
  output [15:0] Output_2
);

  wire clock_1_out;
  wire [2:0] adder_1_out, register_1_q;
  wire [11:0] rom_1_data;

  Register #(.width(3)) register_1 (.D(adder_1_out), .Q(register_1_q), .clk(clock_1_out));  // open: en, clr
  Adder #(.width(3)) adder_1 (.a(register_1_q), .b(3'b001), .out(adder_1_out));  // open: cin, cout
  ROM #(.addrWidth(3), .dataWidth(12)) rom_1 (.addr(register_1_q), .data(rom_1_data));  // open: sel
  Clock clock_1 (.out(clock_1_out));
  _16_Bit_Register_File u_16_bit_register_file_1 (
    .Write_Data(out_3), .Register_Write_2(rom_1_data[11]), .Read_Data_1(Output),
    .Read_Register_1(rom_1_data[8:6]), .Read_Data_2(Output_2), .Read_Register_2(rom_1_data[5:3]),
    .Write_Register(rom_1_data[2:0]), .Register_Write(clock_1_out));
  _16_Bit_ALu u_16_bit_alu_1 (
    .A(Output), .B(Output_2), .in_3(in_1), .Selection_Bit(rom_1_data[10:9]), .out_5(out_3), .C_Out(out_4));

  // Notes on the sheet:
  //   contents of rom_1 (hex, n*v repeats v):
  //   ea1 dba
endmodule

module _16_Bit_Register_File (
  input  [15:0] Write_Data,
  input  [2:0] Read_Register_1,
  input  [2:0] Read_Register_2,
  input  [2:0] Write_Register,
  input  Register_Write,
  input  Register_Write_2,
  output [15:0] Read_Data_1,
  output [15:0] Read_Data_2
);

  wire and_1_out, and_2_out, and_3_out, and_4_out, and_5_out, and_6_out, and_7_out, and_8_out,
       decoder_1_out0, decoder_1_out1, decoder_1_out2, decoder_1_out3, decoder_1_out4, decoder_1_out5,
       decoder_1_out6, decoder_1_out7;
  wire [15:0] R0_q, R1_q, R2_q, R3_q, R4_q, R5_q, R6_q, R7_q;

  Decoder #(.select(3)) decoder_1 (
    .out0(decoder_1_out0), .out1(decoder_1_out1), .out2(decoder_1_out2), .out3(decoder_1_out3),
    .out4(decoder_1_out4), .out5(decoder_1_out5), .out6(decoder_1_out6), .out7(decoder_1_out7),
    .sel(Write_Register));  // open: en
  and and_1 (and_1_out, decoder_1_out0, Register_Write_2);
  and and_2 (and_2_out, decoder_1_out1, Register_Write_2);
  and and_3 (and_3_out, decoder_1_out2, Register_Write_2);
  and and_4 (and_4_out, decoder_1_out3, Register_Write_2);
  and and_5 (and_5_out, Register_Write_2, decoder_1_out4);
  and and_6 (and_6_out, Register_Write_2, decoder_1_out5);
  and and_7 (and_7_out, Register_Write_2, decoder_1_out6);
  and and_8 (and_8_out, Register_Write_2, decoder_1_out7);
  Register #(.width(16)) R0 (.D(Write_Data), .en(and_1_out), .Q(R0_q), .clk(Register_Write));  // open: clr
  Register #(.width(16)) R1 (.D(Write_Data), .en(and_2_out), .Q(R1_q), .clk(Register_Write));  // open: clr
  Register #(.width(16)) R2 (.D(Write_Data), .en(and_3_out), .Q(R2_q), .clk(Register_Write));  // open: clr
  Register #(.width(16)) R3 (.D(Write_Data), .en(and_4_out), .Q(R3_q), .clk(Register_Write));  // open: clr
  Register #(.width(16)) R4 (.D(Write_Data), .en(and_5_out), .Q(R4_q), .clk(Register_Write));  // open: clr
  Register #(.width(16)) R5 (.D(Write_Data), .en(and_6_out), .Q(R5_q), .clk(Register_Write));  // open: clr
  Register #(.width(16)) R6 (.D(Write_Data), .en(and_7_out), .Q(R6_q), .clk(Register_Write));  // open: clr
  Register #(.width(16)) R7 (.D(Write_Data), .en(and_8_out), .Q(R7_q), .clk(Register_Write));  // open: clr
  Multiplexer #(.select(3), .width(16)) multiplexer_1 (
    .in0(R0_q), .in1(R1_q), .in2(R2_q), .in3(R3_q), .in4(R4_q), .in5(R5_q), .in6(R6_q), .in7(R7_q),
    .out(Read_Data_1), .sel(Read_Register_1));  // open: en
  Multiplexer #(.select(3), .width(16)) multiplexer_2 (
    .in0(R0_q), .in1(R1_q), .in2(R2_q), .in3(R3_q), .in4(R4_q), .in5(R5_q), .in6(R6_q), .in7(R7_q),
    .out(Read_Data_2), .sel(Read_Register_2));  // open: en
endmodule

module _1_Bit_Alu (
  input  A,
  input  B,
  input  C_in,
  input  [1:0] Selection_Bit,
  output Alu_Output,
  output out_6
);

  wire adder_1_cout, adder_1_out, and_1_out, or_1_out, subtractor_1_bout, subtractor_1_out;

  and and_1 (and_1_out, A, B);
  or or_1 (or_1_out, A, B);
  Adder #(.width(1)) adder_1 (.a(A), .b(B), .out(adder_1_out), .cin(C_in), .cout(adder_1_cout));
  Subtractor #(.width(1)) subtractor_1 (.a(A), .b(B), .out(subtractor_1_out), .bin(C_in), .bout(subtractor_1_bout));
  Multiplexer #(.select(2)) multiplexer_1 (
    .in0(and_1_out), .in1(or_1_out), .in2(adder_1_out), .in3(subtractor_1_out), .out(Alu_Output),
    .sel(Selection_Bit));  // open: en
  Multiplexer multiplexer_2 (
    .in0(adder_1_cout), .in1(subtractor_1_bout), .out(out_6), .sel(Selection_Bit[0]), .en(Selection_Bit[1]));

  // Notes on the sheet:
  //   Adder
  //   Sub Tractor
endmodule

module _16_Bit_ALu (
  input  [15:0] A,
  input  [15:0] B,
  input  in_3,
  input  [1:0] Selection_Bit,
  output [15:0] out_5,
  output C_Out
);

  wire n1_bit_alu_1_out_6, n1_bit_alu_2_out_6, n1_bit_alu_3_out_6, n1_bit_alu_4_out_6, n1_bit_alu_5_out_6,
       n1_bit_alu_6_out_6, n1_bit_alu_7_out_6, n1_bit_alu_8_out_6, n1_bit_alu_9_out_6, n1_bit_alu_10_out_6,
       n1_bit_alu_11_out_6, n1_bit_alu_12_out_6, n1_bit_alu_13_out_6, n1_bit_alu_14_out_6,
       n1_bit_alu_15_out_6;

  _1_Bit_Alu u_1_bit_alu_1 (
    .A(A[0]), .B(B[0]), .C_in(in_3), .Selection_Bit(Selection_Bit), .Alu_Output(out_5[0]),
    .out_6(n1_bit_alu_1_out_6));
  _1_Bit_Alu u_1_bit_alu_2 (
    .A(A[1]), .B(B[1]), .C_in(n1_bit_alu_1_out_6), .Selection_Bit(Selection_Bit), .Alu_Output(out_5[1]),
    .out_6(n1_bit_alu_2_out_6));
  _1_Bit_Alu u_1_bit_alu_3 (
    .A(A[2]), .B(B[2]), .C_in(n1_bit_alu_2_out_6), .Selection_Bit(Selection_Bit), .Alu_Output(out_5[2]),
    .out_6(n1_bit_alu_3_out_6));
  _1_Bit_Alu u_1_bit_alu_4 (
    .A(A[3]), .B(B[3]), .C_in(n1_bit_alu_3_out_6), .Selection_Bit(Selection_Bit), .Alu_Output(out_5[3]),
    .out_6(n1_bit_alu_4_out_6));
  _1_Bit_Alu u_1_bit_alu_5 (
    .A(A[4]), .B(B[4]), .C_in(n1_bit_alu_4_out_6), .Selection_Bit(Selection_Bit), .Alu_Output(out_5[4]),
    .out_6(n1_bit_alu_5_out_6));
  _1_Bit_Alu u_1_bit_alu_6 (
    .A(A[5]), .B(B[5]), .C_in(n1_bit_alu_5_out_6), .Selection_Bit(Selection_Bit), .Alu_Output(out_5[5]),
    .out_6(n1_bit_alu_6_out_6));
  _1_Bit_Alu u_1_bit_alu_7 (
    .A(A[6]), .B(B[6]), .C_in(n1_bit_alu_6_out_6), .Selection_Bit(Selection_Bit), .Alu_Output(out_5[6]),
    .out_6(n1_bit_alu_7_out_6));
  _1_Bit_Alu u_1_bit_alu_8 (
    .A(A[7]), .B(B[7]), .C_in(n1_bit_alu_7_out_6), .Selection_Bit(Selection_Bit), .Alu_Output(out_5[7]),
    .out_6(n1_bit_alu_8_out_6));
  _1_Bit_Alu u_1_bit_alu_9 (
    .A(A[8]), .B(B[8]), .C_in(n1_bit_alu_8_out_6), .Selection_Bit(Selection_Bit), .Alu_Output(out_5[8]),
    .out_6(n1_bit_alu_9_out_6));
  _1_Bit_Alu u_1_bit_alu_10 (
    .A(A[9]), .B(B[9]), .C_in(n1_bit_alu_9_out_6), .Selection_Bit(Selection_Bit), .Alu_Output(out_5[9]),
    .out_6(n1_bit_alu_10_out_6));
  _1_Bit_Alu u_1_bit_alu_11 (
    .A(A[10]), .B(B[10]), .C_in(n1_bit_alu_10_out_6), .Selection_Bit(Selection_Bit), .Alu_Output(out_5[10]),
    .out_6(n1_bit_alu_11_out_6));
  _1_Bit_Alu u_1_bit_alu_12 (
    .A(A[11]), .B(B[11]), .C_in(n1_bit_alu_11_out_6), .Selection_Bit(Selection_Bit), .Alu_Output(out_5[11]),
    .out_6(n1_bit_alu_12_out_6));
  _1_Bit_Alu u_1_bit_alu_13 (
    .A(A[12]), .B(B[12]), .C_in(n1_bit_alu_12_out_6), .Selection_Bit(Selection_Bit), .Alu_Output(out_5[12]),
    .out_6(n1_bit_alu_13_out_6));
  _1_Bit_Alu u_1_bit_alu_14 (
    .A(A[13]), .B(B[13]), .C_in(n1_bit_alu_13_out_6), .Selection_Bit(Selection_Bit), .Alu_Output(out_5[13]),
    .out_6(n1_bit_alu_14_out_6));
  _1_Bit_Alu u_1_bit_alu_15 (
    .A(A[14]), .B(B[14]), .C_in(n1_bit_alu_14_out_6), .Selection_Bit(Selection_Bit), .Alu_Output(out_5[14]),
    .out_6(n1_bit_alu_15_out_6));
  _1_Bit_Alu u_1_bit_alu_16 (
    .A(A[15]), .B(B[15]), .C_in(n1_bit_alu_15_out_6), .Selection_Bit(Selection_Bit), .Alu_Output(out_5[15]),
    .out_6(C_Out));
endmodule
